// Logisim project CPU.circ as structural Verilog: 9 circuits, main circuit DMEM
module DMEM (
  input  [15:0] ADDRESS,
  input  MemWrite,
  input  clk,
  input  MemRead,
  input  Clear,
  input  [15:0] DATA_IN,
  input  WORD_EN,
  input  ENDIANNESS,
  output [15:0] DATA_OUT
);

  wire dmem_control_1_flip_signal, dmem_control_1_sel_0, dmem_control_1_sel_1;
  wire [7:0] ram_1_data, ram_2_data;
  wire [15:0] byte_mirror_1_out, byte_selector_1_word_out;

  BYTE_MIRROR byte_mirror_1 (.IN(DATA_IN), .EN(dmem_control_1_flip_signal), .OUT(byte_mirror_1_out));
  DMEM_CONTROL dmem_control_1 (
    .ENDIANNESS(ENDIANNESS), .WORD_EN(WORD_EN), .FLIP_SIGNAL(dmem_control_1_flip_signal),
    .SEL_0(dmem_control_1_sel_0), .SEL_1(dmem_control_1_sel_1), .A0(ADDRESS[0]));
  RAM #(.addrWidth(15), .bus("separate")) ram_1 (
    .addr(ADDRESS[15:1]), .din(byte_mirror_1_out[7:0]), .data(ram_1_data), .str(MemWrite),
    .sel(dmem_control_1_sel_0), .clk(clk), .ld(MemRead), .clr(Clear));
  RAM #(.addrWidth(15), .bus("separate")) ram_2 (
    .addr(ADDRESS[15:1]), .din(byte_mirror_1_out[15:8]), .data(ram_2_data), .str(MemWrite),
    .sel(dmem_control_1_sel_1), .clk(clk), .ld(MemRead), .clr(Clear));
  BYTE_SELECTOR byte_selector_1 (
    .BYTE0(ram_1_data), .EN0(dmem_control_1_sel_0), .BYTE1(ram_2_data), .EN1(dmem_control_1_sel_1),
    .WORD_OUT(byte_selector_1_word_out));
  BYTE_MIRROR byte_mirror_2 (.IN(byte_selector_1_word_out), .EN(dmem_control_1_flip_signal), .OUT(DATA_OUT));
endmodule

module BYTE_MIRROR (
  input  [15:0] IN,
  input  EN,
  output [15:0] OUT
);

  Multiplexer #(.width(8), .enable("false")) multiplexer_1 (.in0(IN[7:0]), .in1(IN[15:8]), .out(OUT[7:0]), .sel(EN));
  Multiplexer #(.width(8), .enable("false")) multiplexer_2 (.in0(IN[15:8]), .in1(IN[7:0]), .out(OUT[15:8]), .sel(EN));
endmodule

module BYTE_SELECTOR (
  input  [7:0] BYTE0,
  input  EN0,
  input  [7:0] BYTE1,
  input  EN1,
  output [15:0] WORD_OUT
);

  Multiplexer #(.width(8), .enable("false")) multiplexer_1 (
    .in0({8{1'b0}}), .in1(BYTE0), .out(WORD_OUT[7:0]), .sel(EN0));
  Multiplexer #(.width(8), .enable("false")) multiplexer_2 (
    .in0({8{1'b0}}), .in1(BYTE1), .out(WORD_OUT[15:8]), .sel(EN1));
endmodule

module DMEM_CONTROL (
  input  A0,
  input  WORD_EN,
  input  ENDIANNESS,
  output SEL_0,
  output SEL_1,
  output FLIP_SIGNAL
);

  or or_1 (SEL_0, ~A0, WORD_EN);  // OR_Gate
  or or_2 (SEL_1, A0, WORD_EN);
  Multiplexer #(.enable("false")) multiplexer_1 (.in0(A0), .in1(ENDIANNESS), .out(FLIP_SIGNAL), .sel(WORD_EN));
endmodule

module IMEM (
  input  [15:0] ADDRESS,
  input  [15:0] INSTRUCTION_IN,
  input  MemWrite,
  input  clk,
  input  MemRead,
  input  Clear,
  output [15:0] INSTRUCTION_OUT
);

  RAM #(.addrWidth(15), .dataWidth(16), .bus("separate")) ram_1 (
    .addr(ADDRESS[15:1]), .din(INSTRUCTION_IN), .data(INSTRUCTION_OUT), .str(MemWrite), .sel(1'b1),
    .clk(clk), .ld(MemRead), .clr(Clear));
endmodule

module ALU (
  input  [2:0] OPERATION,
  input  [15:0] OPERAND_1,
  input  [15:0] OPERAND_2,
  output [15:0] ALU_RES,
  output carry,
  output borrow,
  output greater,
  output zero,
  output less
);

  wire adder_1_cout, comparator_1_eq, comparator_1_gt, comparator_1_lt, decoder_1_out0, decoder_1_out1,
       decoder_1_out2, decoder_1_out3, decoder_1_out4, subtractor_1_bout;
  wire [15:0] adder_1_out, and_1_out, or_1_out, subtractor_1_out;

  assign ALU_RES = decoder_1_out0 ? and_1_out : 16'bz;  // Controlled_Buffer controlled_buffer_1
  assign and_1_out = OPERAND_1 & OPERAND_2;  // AND_Gate and_1, 16 bits wide
  assign or_1_out = OPERAND_1 | OPERAND_2;  // OR_Gate or_1, 16 bits wide
  assign ALU_RES = decoder_1_out1 ? or_1_out : 16'bz;  // Controlled_Buffer controlled_buffer_2
  Adder #(.width(16)) adder_1 (.a(OPERAND_1), .b(OPERAND_2), .out(adder_1_out), .cin(1'b0), .cout(adder_1_cout));
  assign ALU_RES = decoder_1_out2 ? adder_1_out : 16'bz;  // Controlled_Buffer controlled_buffer_3
  assign carry = decoder_1_out2 ? adder_1_cout : 1'bz;  // Controlled_Buffer controlled_buffer_4
  assign ALU_RES = decoder_1_out3 ? subtractor_1_out : 16'bz;  // Controlled_Buffer controlled_buffer_5
  Subtractor #(.width(16)) subtractor_1 (
    .a(OPERAND_1), .b(OPERAND_2), .out(subtractor_1_out), .bin(1'b0), .bout(subtractor_1_bout));
  assign borrow = decoder_1_out3 ? subtractor_1_bout : 1'bz;  // Controlled_Buffer controlled_buffer_6
  assign greater = decoder_1_out4 ? comparator_1_gt : 1'bz;  // Controlled_Buffer controlled_buffer_7
  Comparator #(.width(16)) comparator_1 (
    .a(OPERAND_1), .b(OPERAND_2), .gt(comparator_1_gt), .eq(comparator_1_eq), .lt(comparator_1_lt));
  assign zero = decoder_1_out4 ? comparator_1_eq : 1'bz;  // Controlled_Buffer controlled_buffer_8
  assign less = decoder_1_out4 ? comparator_1_lt : 1'bz;  // Controlled_Buffer controlled_buffer_9
  Decoder #(.select(3), .enable("false")) decoder_1 (
    .out0(decoder_1_out0), .out1(decoder_1_out1), .out2(decoder_1_out2), .out3(decoder_1_out3),
    .out4(decoder_1_out4), .sel(OPERATION));  // open: out5, out6, out7
endmodule

module REG_FILE (
  input  [15:0] Write_data,
  input  [2:0] read_register_1,
  input  [2:0] Write_register,
  input  [2:0] read_register_2,
  input  RegWrite,
  input  clk,
  output [15:0] read_data_1,
  output [15:0] read_data_2
);

  wire and_1_out, and_2_out, and_3_out, and_4_out, and_5_out, and_6_out, and_7_out, decoder_1_out1,
       decoder_1_out2, decoder_1_out3, decoder_1_out4, decoder_1_out5, decoder_1_out6, decoder_1_out7;
  wire [15:0] register_1_q, register_2_q, register_3_q, register_4_q, register_5_q, register_6_q,
       register_7_q;

  Decoder #(.select(3), .enable("false")) decoder_1 (
    .out1(decoder_1_out1), .out2(decoder_1_out2), .out3(decoder_1_out3), .out4(decoder_1_out4),
    .out5(decoder_1_out5), .out6(decoder_1_out6), .out7(decoder_1_out7), .sel(Write_register));  // open: out0
  and and_1 (and_1_out, decoder_1_out1, RegWrite);
  and and_2 (and_2_out, decoder_1_out2, RegWrite);
  and and_3 (and_3_out, decoder_1_out3, RegWrite);
  and and_4 (and_4_out, decoder_1_out4, RegWrite);
  and and_5 (and_5_out, decoder_1_out5, RegWrite);
  and and_6 (and_6_out, decoder_1_out6, RegWrite);
  and and_7 (and_7_out, decoder_1_out7, RegWrite);
  Register #(.width(16)) register_1 (.D(Write_data), .Q(register_1_q), .clk(clk), .clr(and_1_out));  // open: en
  Register #(.width(16)) register_2 (.D(Write_data), .Q(register_2_q), .clk(clk), .clr(and_2_out));  // open: en
  Register #(.width(16)) register_3 (.D(Write_data), .Q(register_3_q), .clk(clk), .clr(and_3_out));  // open: en
  Register #(.width(16)) register_4 (.D(Write_data), .Q(register_4_q), .clk(clk), .clr(and_4_out));  // open: en
  Register #(.width(16)) register_5 (.D(Write_data), .Q(register_5_q), .clk(clk), .clr(and_5_out));  // open: en
  Register #(.width(16)) register_6 (.D(Write_data), .Q(register_6_q), .clk(clk), .clr(and_6_out));  // open: en
  Register #(.width(16)) register_7 (.D(Write_data), .Q(register_7_q), .clk(clk), .clr(and_7_out));  // open: en
  Multiplexer #(.select(3), .width(16), .enable("false")) multiplexer_1 (
    .in0({16{1'b0}}), .in1(register_1_q), .in2(register_2_q), .in3(register_3_q), .in4(register_4_q),
    .in5(register_5_q), .in6(register_6_q), .in7(register_7_q), .out(read_data_1), .sel(read_register_1));
  Multiplexer #(.select(3), .width(16), .enable("false")) multiplexer_2 (
    .in0({16{1'b0}}), .in1(register_1_q), .in2(register_2_q), .in3(register_3_q), .in4(register_4_q),
    .in5(register_5_q), .in6(register_6_q), .in7(register_7_q), .out(read_data_2), .sel(read_register_2));
endmodule

module EXTENDER (
  input  [5:0] Imm6,
  input  ExtOp,
  output [15:0] ExtOutput
);

  wire [15:0] bit_extender_1_out, bit_extender_2_out;

  assign bit_extender_1_out = {{10{1'b0}}, Imm6};  // Bit_Extender bit_extender_1
  assign bit_extender_2_out = {{10{Imm6[5]}}, Imm6};  // Bit_Extender bit_extender_2
  Multiplexer #(.width(16), .enable("false")) multiplexer_1 (
    .in0(bit_extender_1_out), .in1(bit_extender_2_out), .out(ExtOutput), .sel(ExtOp));
endmodule

module FORWARDING_UNIT (
  input  EX_MEM_RegWrite,
  input  [2:0] EX_MEM_RegisterRd,
  input  [2:0] ID_EX_RegisterRs,
  input  [2:0] ID_EX_RegisterRt,
  input  MEM_WB_RegWrite,
  input  [2:0] MEM_WB_RegisterRd,
  output [1:0] ForwardA,
  output [1:0] ForwardB
);

  wire and_1_out, and_2_out, and_3_out, and_4_out, and_5_out, and_6_out, and_7_out, and_8_out, and_9_out,
       and_10_out, or_1_out, or_2_out;
  wire [2:0] xnor_1_out, xnor_2_out, xnor_3_out, xnor_4_out;

  or or_1 (or_1_out, EX_MEM_RegisterRd[0], EX_MEM_RegisterRd[1], EX_MEM_RegisterRd[2]);
  assign xnor_1_out = ~(ID_EX_RegisterRs ^ EX_MEM_RegisterRd);  // XNOR_Gate xnor_1, 3 bits wide
  assign xnor_2_out = ~(ID_EX_RegisterRt ^ EX_MEM_RegisterRd);  // XNOR_Gate xnor_2, 3 bits wide
  or or_2 (or_2_out, MEM_WB_RegisterRd[0], MEM_WB_RegisterRd[1], MEM_WB_RegisterRd[2]);
  assign xnor_3_out = ~(ID_EX_RegisterRs ^ MEM_WB_RegisterRd);  // XNOR_Gate xnor_3, 3 bits wide
  assign xnor_4_out = ~(ID_EX_RegisterRt ^ MEM_WB_RegisterRd);  // XNOR_Gate xnor_4, 3 bits wide
  and and_1 (and_1_out, EX_MEM_RegWrite, or_1_out);
  and and_2 (and_2_out, xnor_1_out[0], xnor_1_out[1], xnor_1_out[2]);
  and and_3 (and_3_out, xnor_2_out[0], xnor_2_out[1], xnor_2_out[2]);
  and and_4 (and_4_out, MEM_WB_RegWrite, or_2_out);
  and and_5 (and_5_out, xnor_3_out[0], xnor_3_out[1], xnor_3_out[2]);
  and and_6 (and_6_out, xnor_4_out[0], xnor_4_out[1], xnor_4_out[2]);
  and and_7 (and_7_out, and_1_out, and_2_out);
  and and_8 (and_8_out, and_1_out, and_3_out);
  and and_9 (and_9_out, and_4_out, and_5_out);
  and and_10 (and_10_out, and_4_out, and_6_out);
  Priority_Encoder #(.select(2)) priority_encoder_1 (
    .in1(and_9_out), .in2(and_7_out), .out(ForwardA));  // open: in0, in3, gs, en_out, en_in
  Priority_Encoder #(.select(2)) priority_encoder_2 (
    .in1(and_10_out), .in2(and_8_out), .out(ForwardB));  // open: in0, in3, gs, en_out, en_in
endmodule
