// Logisim project IMEM.circ as structural Verilog: 1 circuit, main circuit main
module main (
  input  [15:0] ADDRESS,
  input  ENDIANESS,
  output [15:0] INSTRUCTION
);

  wire multiplexer_4_out, not_1_out, or_1_out, or_2_out;
  wire [7:0] multiplexer_1_out, multiplexer_2_out, rom_1_data, rom_2_data;

  not not_1 (not_1_out, ADDRESS[0]);
  or or_1 (or_1_out, not_1_out, 1'b1);
  or or_2 (or_2_out, ADDRESS[0], 1'b1);
  ROM #(.addrWidth(15)) rom_1 (.addr(ADDRESS[15:1]), .data(rom_1_data), .sel(or_1_out));
  ROM #(.addrWidth(15)) rom_2 (.addr(ADDRESS[15:1]), .data(rom_2_data), .sel(or_2_out));
  Multiplexer #(.width(8), .enable("false")) multiplexer_1 (
    .in0({8{1'b0}}), .in1(rom_1_data), .out(multiplexer_1_out), .sel(or_1_out));
  Multiplexer #(.width(8), .enable("false")) multiplexer_2 (
    .in0({8{1'b0}}), .in1(rom_2_data), .out(multiplexer_2_out), .sel(or_2_out));
  Multiplexer #(.width(16), .enable("false")) multiplexer_3 (
    .in0({multiplexer_2_out, multiplexer_1_out}), .in1({multiplexer_1_out, multiplexer_2_out}),
    .out(INSTRUCTION), .sel(multiplexer_4_out));
  Multiplexer #(.enable("false")) multiplexer_4 (
    .in0(ADDRESS[0]), .in1(ENDIANESS), .out(multiplexer_4_out), .sel(1'b1));
endmodule
