// Logisim project Pipelined-MIPS-CPU.circ as structural Verilog: 17 circuits, main circuit DMEM
module DMEM (
  input  [15:0] ADDRESS,
  input  MemWrite,
  input  clk,
  input  MemRead,
  input  Clear,
  input  [15:0] DATA_IN,
  input  WORD_EN,
  input  ENDIANNESS,
  output [15:0] DATA_OUT
);

  wire dmem_control_1_flip_signal, dmem_control_1_sel_0, dmem_control_1_sel_1, not_1_out;
  wire [7:0] ram_1_data, ram_2_data;
  wire [15:0] byte_mirror_1_out, byte_selector_1_word_out;

  not not_1 (not_1_out, clk);
  BYTE_MIRROR byte_mirror_1 (.IN(DATA_IN), .EN(dmem_control_1_flip_signal), .OUT(byte_mirror_1_out));
  DMEM_CONTROL dmem_control_1 (
    .ENDIANNESS(ENDIANNESS), .WORD_EN(WORD_EN), .FLIP_SIGNAL(dmem_control_1_flip_signal),
    .SEL_0(dmem_control_1_sel_0), .SEL_1(dmem_control_1_sel_1), .A0(ADDRESS[0]));
  RAM #(.addrWidth(15), .bus("separate")) ram_1 (
    .addr(ADDRESS[15:1]), .din(byte_mirror_1_out[7:0]), .data(ram_1_data), .str(MemWrite),
    .sel(dmem_control_1_sel_0), .clk(not_1_out), .ld(MemRead), .clr(Clear));
  RAM #(.addrWidth(15), .bus("separate")) ram_2 (
    .addr(ADDRESS[15:1]), .din(byte_mirror_1_out[15:8]), .data(ram_2_data), .str(MemWrite),
    .sel(dmem_control_1_sel_1), .clk(not_1_out), .ld(MemRead), .clr(Clear));
  BYTE_SELECTOR byte_selector_1 (
    .BYTE0(ram_1_data), .EN0(dmem_control_1_sel_0), .BYTE1(ram_2_data), .EN1(dmem_control_1_sel_1),
    .WORD_OUT(byte_selector_1_word_out));
  BYTE_MIRROR byte_mirror_2 (.IN(byte_selector_1_word_out), .EN(dmem_control_1_flip_signal), .OUT(DATA_OUT));
endmodule

module BYTE_MIRROR (
  input  [15:0] IN,
  input  EN,
  output [15:0] OUT
);

  Multiplexer #(.width(8), .enable("false")) multiplexer_1 (.in0(IN[7:0]), .in1(IN[15:8]), .out(OUT[7:0]), .sel(EN));
  Multiplexer #(.width(8), .enable("false")) multiplexer_2 (.in0(IN[15:8]), .in1(IN[7:0]), .out(OUT[15:8]), .sel(EN));
endmodule

module BYTE_SELECTOR (
  input  [7:0] BYTE0,
  input  EN0,
  input  [7:0] BYTE1,
  input  EN1,
  output [15:0] WORD_OUT
);

  Multiplexer #(.width(8), .enable("false")) multiplexer_1 (
    .in0({8{1'b0}}), .in1(BYTE0), .out(WORD_OUT[7:0]), .sel(EN0));
  Multiplexer #(.width(8), .enable("false")) multiplexer_2 (
    .in0({8{1'b0}}), .in1(BYTE1), .out(WORD_OUT[15:8]), .sel(EN1));
endmodule

module DMEM_CONTROL (
  input  A0,
  input  WORD_EN,
  input  ENDIANNESS,
  output SEL_0,
  output SEL_1,
  output FLIP_SIGNAL
);

  or or_1 (SEL_0, ~A0, WORD_EN);  // OR_Gate
  or or_2 (SEL_1, A0, WORD_EN);
  Multiplexer #(.enable("false")) multiplexer_1 (.in0(A0), .in1(ENDIANNESS), .out(FLIP_SIGNAL), .sel(WORD_EN));
endmodule

module IMEM (
  input  [15:0] ADDRESS,
  input  [15:0] INSTRUCTION_IN,
  input  MemWrite,
  input  clk,
  input  MemRead,
  input  Clear,
  output [15:0] INSTRUCTION_OUT
);

  wire not_1_out;

  not not_1 (not_1_out, clk);
  RAM #(.addrWidth(15), .dataWidth(16), .bus("separate")) ram_1 (
    .addr(ADDRESS[15:1]), .din(INSTRUCTION_IN), .data(INSTRUCTION_OUT), .str(MemWrite), .sel(1'b1),
    .clk(not_1_out), .ld(MemRead), .clr(Clear));
endmodule

module ALU (
  input  [2:0] OPERATION,
  input  [15:0] OPERAND_1,
  input  [15:0] OPERAND_2,
  output [15:0] ALU_RES,
  output carry,
  output borrow,
  output greater,
  output zero,
  output less
);

  wire adder_1_cout, comparator_1_eq, comparator_1_gt, comparator_1_lt, decoder_1_out0, decoder_1_out1,
       decoder_1_out2, decoder_1_out3, decoder_1_out4, decoder_1_out5, decoder_1_out6, decoder_1_out7,
       subtractor_1_bout;
  wire [15:0] adder_1_out, and_1_out, not_1_out, or_1_out, shifter_1_out, shifter_2_out, subtractor_1_out;

  assign not_1_out = ~OPERAND_1;  // NOT_Gate not_1, 16 bits wide
  assign ALU_RES = decoder_1_out0 ? and_1_out : 16'bz;  // Controlled_Buffer controlled_buffer_1
  assign and_1_out = OPERAND_1 & OPERAND_2;  // AND_Gate and_1, 16 bits wide
  assign or_1_out = OPERAND_1 | OPERAND_2;  // OR_Gate or_1, 16 bits wide
  assign ALU_RES = decoder_1_out1 ? or_1_out : 16'bz;  // Controlled_Buffer controlled_buffer_2
  Adder #(.width(16)) adder_1 (.a(OPERAND_1), .b(OPERAND_2), .out(adder_1_out), .cin(1'b0), .cout(adder_1_cout));
  assign ALU_RES = decoder_1_out2 ? adder_1_out : 16'bz;  // Controlled_Buffer controlled_buffer_3
  assign carry = decoder_1_out2 ? adder_1_cout : 1'bz;  // Controlled_Buffer controlled_buffer_4
  Subtractor #(.width(16)) subtractor_1 (
    .a(OPERAND_1), .b(OPERAND_2), .out(subtractor_1_out), .bin(1'b0), .bout(subtractor_1_bout));
  assign ALU_RES = decoder_1_out3 ? subtractor_1_out : 16'bz;  // Controlled_Buffer controlled_buffer_5
  assign borrow = decoder_1_out3 ? subtractor_1_bout : 1'bz;  // Controlled_Buffer controlled_buffer_6
  assign greater = decoder_1_out4 ? comparator_1_gt : 1'bz;  // Controlled_Buffer controlled_buffer_7
  Comparator #(.width(16)) comparator_1 (
    .a(OPERAND_1), .b(OPERAND_2), .gt(comparator_1_gt), .eq(comparator_1_eq), .lt(comparator_1_lt));
  assign zero = decoder_1_out4 ? comparator_1_eq : 1'bz;  // Controlled_Buffer controlled_buffer_8
  assign less = decoder_1_out4 ? comparator_1_lt : 1'bz;  // Controlled_Buffer controlled_buffer_9
  assign ALU_RES = decoder_1_out5 ? not_1_out : 16'bz;  // Controlled_Buffer controlled_buffer_10
  Shifter #(.width(16)) shifter_1 (.in(OPERAND_1), .\dist (OPERAND_2[3:0]), .out(shifter_1_out));
  assign ALU_RES = decoder_1_out6 ? shifter_1_out : 16'bz;  // Controlled_Buffer controlled_buffer_11
  Shifter #(.width(16), .shift("lr")) shifter_2 (.in(OPERAND_1), .\dist (OPERAND_2[3:0]), .out(shifter_2_out));
  assign ALU_RES = decoder_1_out7 ? shifter_2_out : 16'bz;  // Controlled_Buffer controlled_buffer_12
  Decoder #(.select(3), .enable("false")) decoder_1 (
    .out0(decoder_1_out0), .out1(decoder_1_out1), .out2(decoder_1_out2), .out3(decoder_1_out3),
    .out4(decoder_1_out4), .out5(decoder_1_out5), .out6(decoder_1_out6), .out7(decoder_1_out7),
    .sel(OPERATION));
endmodule

module REG_FILE (
  input  [15:0] Write_data,
  input  [2:0] read_register_1,
  input  [2:0] Write_register,
  input  [2:0] read_register_2,
  input  RegWrite,
  input  clk,
  input  Clear,
  output [15:0] read_data_1,
  output [15:0] read_data_2
);

  wire and_1_out, and_2_out, and_3_out, and_4_out, and_5_out, and_6_out, and_7_out, decoder_1_out1,
       decoder_1_out2, decoder_1_out3, decoder_1_out4, decoder_1_out5, decoder_1_out6, decoder_1_out7;
  wire [15:0] register_1_q, register_2_q, register_3_q, register_4_q, register_5_q, register_6_q,
       register_7_q;

  Decoder #(.select(3), .enable("false")) decoder_1 (
    .out1(decoder_1_out1), .out2(decoder_1_out2), .out3(decoder_1_out3), .out4(decoder_1_out4),
    .out5(decoder_1_out5), .out6(decoder_1_out6), .out7(decoder_1_out7), .sel(Write_register));  // open: out0
  and and_1 (and_1_out, decoder_1_out1, RegWrite);
  and and_2 (and_2_out, decoder_1_out2, RegWrite);
  and and_3 (and_3_out, decoder_1_out3, RegWrite);
  and and_4 (and_4_out, decoder_1_out4, RegWrite);
  and and_5 (and_5_out, decoder_1_out5, RegWrite);
  and and_6 (and_6_out, decoder_1_out6, RegWrite);
  and and_7 (and_7_out, decoder_1_out7, RegWrite);
  Register #(.width(16)) register_1 (.D(Write_data), .en(and_1_out), .Q(register_1_q), .clk(clk), .clr(Clear));
  Register #(.width(16)) register_2 (.D(Write_data), .en(and_2_out), .Q(register_2_q), .clk(clk), .clr(Clear));
  Register #(.width(16)) register_3 (.D(Write_data), .en(and_3_out), .Q(register_3_q), .clk(clk), .clr(Clear));
  Register #(.width(16)) register_4 (.D(Write_data), .en(and_4_out), .Q(register_4_q), .clk(clk), .clr(Clear));
  Register #(.width(16)) register_5 (.D(Write_data), .en(and_5_out), .Q(register_5_q), .clk(clk), .clr(Clear));
  Register #(.width(16)) register_6 (.D(Write_data), .en(and_6_out), .Q(register_6_q), .clk(clk), .clr(Clear));
  Register #(.width(16)) register_7 (.D(Write_data), .en(and_7_out), .Q(register_7_q), .clk(clk), .clr(Clear));
  Multiplexer #(.select(3), .width(16), .enable("false")) multiplexer_1 (
    .in0({16{1'b0}}), .in1(register_1_q), .in2(register_2_q), .in3(register_3_q), .in4(register_4_q),
    .in5(register_5_q), .in6(register_6_q), .in7(register_7_q), .out(read_data_1), .sel(read_register_1));
  Multiplexer #(.select(3), .width(16), .enable("false")) multiplexer_2 (
    .in0({16{1'b0}}), .in1(register_1_q), .in2(register_2_q), .in3(register_3_q), .in4(register_4_q),
    .in5(register_5_q), .in6(register_6_q), .in7(register_7_q), .out(read_data_2), .sel(read_register_2));
endmodule

module EXTENDER6 (
  input  [5:0] Imm6,
  input  ExtOp,
  output [15:0] ExtOutput
);

  wire [15:0] bit_extender_1_out, bit_extender_2_out;

  assign bit_extender_1_out = {{10{1'b0}}, Imm6};  // Bit_Extender bit_extender_1
  assign bit_extender_2_out = {{10{Imm6[5]}}, Imm6};  // Bit_Extender bit_extender_2
  Multiplexer #(.width(16), .enable("false")) multiplexer_1 (
    .in0(bit_extender_1_out), .in1(bit_extender_2_out), .out(ExtOutput), .sel(ExtOp));
endmodule

module FORWARDING_UNIT (
  input  MEM_WB_RegWrite,
  input  [2:0] MEM_WB_RegisterRd,
  input  [2:0] ID_RegisterRs,
  input  [2:0] ID_RegisterRt,
  input  [15:0] MEM_WB_Rd,
  input  EX_MEM_MemRead,
  input  EX_MEM_MemWrite,
  input  [15:0] EX_MEM_Rd,
  input  EX_MEM_RegWrite,
  input  [2:0] EX_MEM_RegisterRd,
  input  [2:0] EX_OP1,
  input  [2:0] EX_OP2,
  input  [2:0] EX_RegisterRd,
  input  EX_MemWrite,
  output ID_ForwardRs,
  output ID_ForwardRt,
  output [15:0] ID_Rs,
  output [15:0] ID_Rt,
  output EX_ForwardOP1,
  output EX_ForwardOP2,
  output [15:0] EX_OP1_2,
  output [15:0] EX_OP2_2,
  output EX_ForwardRD,
  output [15:0] EX_RD,
  output MEM_ForwardDataIn,
  output [15:0] MEM_DATA_IN
);

  wire and_1_out, and_2_out, and_3_out, and_4_out, and_5_out, and_6_out, and_7_out, and_8_out, and_9_out,
       and_10_out, and_11_out, and_12_out, and_13_out, and_14_out, and_15_out, and_16_out, and_17_out,
       and_18_out, and_19_out, and_20_out, and_21_out, and_23_out, and_24_out, or_1_out, or_2_out, or_3_out,
       or_4_out, or_5_out, priority_encoder_1_out, priority_encoder_2_out, priority_encoder_3_out,
       priority_encoder_4_out;
  wire [2:0] xnor_1_out, xnor_2_out, xnor_3_out, xnor_4_out, xnor_5_out, xnor_6_out, xnor_7_out, xnor_8_out,
       xnor_9_out, xnor_10_out;

  or or_1 (or_1_out, MEM_WB_RegisterRd[0], MEM_WB_RegisterRd[1], MEM_WB_RegisterRd[2]);
  assign xnor_1_out = ~(ID_RegisterRs ^ MEM_WB_RegisterRd);  // XNOR_Gate xnor_1, 3 bits wide
  assign xnor_2_out = ~(ID_RegisterRt ^ MEM_WB_RegisterRd);  // XNOR_Gate xnor_2, 3 bits wide
  or or_2 (or_2_out, EX_MEM_RegisterRd[0], EX_MEM_RegisterRd[1], EX_MEM_RegisterRd[2]);
  assign xnor_3_out = ~(ID_RegisterRs ^ EX_MEM_RegisterRd);  // XNOR_Gate xnor_3, 3 bits wide
  assign xnor_4_out = ~(ID_RegisterRt ^ EX_MEM_RegisterRd);  // XNOR_Gate xnor_4, 3 bits wide
  or or_3 (or_3_out, MEM_WB_RegisterRd[0], MEM_WB_RegisterRd[1], MEM_WB_RegisterRd[2]);
  assign xnor_5_out = ~(EX_OP1 ^ MEM_WB_RegisterRd);  // XNOR_Gate xnor_5, 3 bits wide
  assign xnor_6_out = ~(EX_OP2 ^ MEM_WB_RegisterRd);  // XNOR_Gate xnor_6, 3 bits wide
  assign xnor_7_out = ~(EX_RegisterRd ^ MEM_WB_RegisterRd);  // XNOR_Gate xnor_7, 3 bits wide
  or or_4 (or_4_out, EX_MEM_RegisterRd[0], EX_MEM_RegisterRd[1], EX_MEM_RegisterRd[2]);
  assign xnor_8_out = ~(EX_OP1 ^ EX_MEM_RegisterRd);  // XNOR_Gate xnor_8, 3 bits wide
  assign xnor_9_out = ~(EX_OP2 ^ EX_MEM_RegisterRd);  // XNOR_Gate xnor_9, 3 bits wide
  or or_5 (or_5_out, MEM_WB_RegisterRd[0], MEM_WB_RegisterRd[1], MEM_WB_RegisterRd[2]);
  assign xnor_10_out = ~(EX_MEM_RegisterRd ^ MEM_WB_RegisterRd);  // XNOR_Gate xnor_10, 3 bits wide
  and and_1 (and_1_out, MEM_WB_RegWrite, or_1_out);
  and and_2 (and_2_out, xnor_1_out[0], xnor_1_out[1], xnor_1_out[2]);
  and and_3 (and_3_out, xnor_2_out[0], xnor_2_out[1], xnor_2_out[2]);
  and and_4 (and_4_out, ~EX_MEM_MemRead, ~EX_MEM_MemWrite, or_2_out, EX_MEM_RegWrite);  // AND_Gate
  and and_5 (and_5_out, xnor_3_out[0], xnor_3_out[1], xnor_3_out[2]);
  and and_6 (and_6_out, xnor_4_out[0], xnor_4_out[1], xnor_4_out[2]);
  and and_7 (and_7_out, MEM_WB_RegWrite, or_3_out);
  and and_8 (and_8_out, xnor_5_out[0], xnor_5_out[1], xnor_5_out[2]);
  and and_9 (and_9_out, xnor_6_out[0], xnor_6_out[1], xnor_6_out[2]);
  and and_10 (and_10_out, xnor_7_out[0], xnor_7_out[1], xnor_7_out[2]);
  and and_11 (and_11_out, ~EX_MEM_MemRead, ~EX_MEM_MemWrite, or_4_out, EX_MEM_RegWrite);  // AND_Gate
  and and_12 (and_12_out, xnor_8_out[0], xnor_8_out[1], xnor_8_out[2]);
  and and_13 (and_13_out, xnor_9_out[0], xnor_9_out[1], xnor_9_out[2]);
  and and_14 (and_14_out, MEM_WB_RegWrite, or_5_out);
  and and_15 (and_15_out, xnor_10_out[0], xnor_10_out[1], xnor_10_out[2]);
  and and_16 (and_16_out, and_1_out, and_2_out);
  and and_17 (and_17_out, and_1_out, and_3_out);
  and and_18 (and_18_out, and_4_out, and_5_out);
  and and_19 (and_19_out, and_4_out, and_6_out);
  and and_20 (and_20_out, and_7_out, and_8_out);
  and and_21 (and_21_out, and_7_out, and_9_out);
  and and_22 (EX_ForwardRD, and_7_out, EX_MemWrite, and_10_out);
  and and_23 (and_23_out, and_11_out, and_12_out);
  and and_24 (and_24_out, and_11_out, and_13_out);
  and and_25 (MEM_ForwardDataIn, and_14_out, and_15_out);
  Priority_Encoder #(.select(1)) priority_encoder_1 (
    .in0(and_16_out), .in1(and_18_out), .out(priority_encoder_1_out), .gs(ID_ForwardRs));  // open: en_out, en_in
  Priority_Encoder #(.select(1)) priority_encoder_2 (
    .in0(and_17_out), .in1(and_19_out), .out(priority_encoder_2_out), .gs(ID_ForwardRt));  // open: en_out, en_in
  Priority_Encoder #(.select(1)) priority_encoder_3 (
    .in0(and_20_out), .in1(and_23_out), .out(priority_encoder_3_out), .gs(EX_ForwardOP1));  // open: en_out, en_in
  Priority_Encoder #(.select(1)) priority_encoder_4 (
    .in0(and_21_out), .in1(and_24_out), .out(priority_encoder_4_out), .gs(EX_ForwardOP2));  // open: en_out, en_in
  Multiplexer #(.width(16), .enable("false")) multiplexer_1 (
    .in0(MEM_WB_Rd), .in1(EX_MEM_Rd), .out(ID_Rs), .sel(priority_encoder_1_out));
  Multiplexer #(.width(16), .enable("false")) multiplexer_2 (
    .in0(MEM_WB_Rd), .in1(EX_MEM_Rd), .out(ID_Rt), .sel(priority_encoder_2_out));
  Multiplexer #(.width(16), .enable("false")) multiplexer_3 (
    .in0(MEM_WB_Rd), .in1(EX_MEM_Rd), .out(EX_OP1_2), .sel(priority_encoder_3_out));
  Multiplexer #(.width(16), .enable("false")) multiplexer_4 (
    .in0(MEM_WB_Rd), .in1(EX_MEM_Rd), .out(EX_OP2_2), .sel(priority_encoder_4_out));

  assign EX_RD = MEM_WB_Rd;
  assign MEM_DATA_IN = MEM_WB_Rd;
endmodule

module CONTROL_UNIT (
  input  ZERO,
  input  [15:0] Instruction,
  input  IF_flush,
  output JReg,
  output MemRead,
  output Upper,
  output MemtoReg,
  output MemWrite,
  output SLT,
  output CAS,
  output [2:0] AluOpc,
  output BEQ,
  output RegWrite,
  output LINK,
  output ExtOp,
  output [1:0] RegDst,
  output LUI,
  output RS_EN,
  output OP1_IMM12,
  output RT_EN,
  output OP2_IMM6,
  output [1:0] PCSrc,
  output JUMP,
  output Word_EN
);

  wire and_1_out, and_2_out, and_3_out, and_4_out, and_5_out, and_12_out, decoder_1_out0, decoder_1_out1,
       decoder_1_out2, decoder_1_out3, decoder_1_out4, decoder_1_out6, decoder_1_out7, decoder_1_out8,
       decoder_1_out10, decoder_1_out11, decoder_1_out13, decoder_1_out14, decoder_1_out15, decoder_2_out2,
       decoder_2_out3, decoder_2_out4, decoder_2_out6, decoder_2_out7, nor_1_out, not_1_out, or_2_out,
       or_3_out, or_4_out, or_5_out, or_6_out, or_7_out, or_8_out, or_9_out, or_10_out, or_11_out;

  and and_1 (and_1_out, ~Instruction[6], ~Instruction[7], ~Instruction[8]);  // AND_Gate
  and and_2 (and_2_out, ~Instruction[3], ~Instruction[4], ~Instruction[5]);  // AND_Gate
  and and_3 (and_3_out, Instruction[6], ~Instruction[7], ~Instruction[8]);  // AND_Gate
  and and_4 (and_4_out, and_1_out, JReg, and_2_out);
  and and_5 (and_5_out, and_2_out, JReg, and_3_out);
  Decoder #(.select(4), .enable("false")) decoder_1 (
    .out0(decoder_1_out0), .out1(decoder_1_out1), .out2(decoder_1_out2), .out3(decoder_1_out3),
    .out4(decoder_1_out4), .out5(Upper), .out6(decoder_1_out6), .out7(decoder_1_out7), .out8(decoder_1_out8),
    .out9(BEQ), .out10(decoder_1_out10), .out11(decoder_1_out11), .out12(LUI), .out13(decoder_1_out13),
    .out14(decoder_1_out14), .out15(decoder_1_out15), .sel(Instruction[15:12]));
  or or_1 (OP2_IMM6, decoder_1_out1, decoder_1_out2, decoder_1_out3, decoder_1_out4, Upper, decoder_1_out6, decoder_1_out7, decoder_1_out8, BEQ, decoder_1_out14, decoder_1_out15);
  Decoder #(.select(3), .disabled(0)) decoder_2 (
    .out0(JReg), .out1(SLT), .out2(decoder_2_out2), .out3(decoder_2_out3), .out4(decoder_2_out4), .out5(CAS),
    .out6(decoder_2_out6), .out7(decoder_2_out7), .sel(Instruction[2:0]), .en(decoder_1_out0));
  or or_2 (or_2_out, decoder_1_out4, Upper, decoder_1_out6, decoder_2_out4);
  or or_3 (or_3_out, decoder_1_out7, decoder_1_out8);
  and and_6 (MemRead, ~IF_flush, or_2_out);  // AND_Gate
  and and_7 (MemWrite, ~IF_flush, or_3_out);  // AND_Gate
  or or_4 (or_4_out, decoder_2_out7, decoder_1_out1);
  or or_5 (or_5_out, decoder_2_out6, decoder_1_out2);
  or or_6 (or_6_out, decoder_1_out3, MemWrite, decoder_2_out3, MemRead);
  or or_7 (or_7_out, CAS, SLT);
  nor nor_1 (nor_1_out, and_4_out, decoder_1_out7, decoder_1_out8, BEQ, decoder_1_out10);
  or or_8 (or_8_out, decoder_1_out11, LUI, decoder_1_out10);
  or or_9 (or_9_out, decoder_1_out11, and_5_out);
  or or_10 (or_10_out, decoder_1_out11, decoder_1_out10, and_5_out, and_4_out);
  or or_11 (or_11_out, decoder_1_out14, LUI);
  and and_8 (RegWrite, ~IF_flush, nor_1_out);  // AND_Gate
  nor nor_2 (ExtOp, decoder_1_out1, decoder_1_out2);
  and and_9 (OP1_IMM12, ~IF_flush, or_8_out);  // AND_Gate
  and and_10 (LINK, ~IF_flush, or_9_out);  // AND_Gate
  and and_11 (JUMP, ~IF_flush, or_10_out);  // AND_Gate
  Priority_Encoder priority_encoder_1 (
    .in0(or_4_out), .in1(or_5_out), .in2(or_6_out), .in3(decoder_2_out2), .in4(or_7_out),
    .in5(decoder_1_out13), .in6(or_11_out), .in7(decoder_1_out15), .out(AluOpc));  // open: en_in, gs, en_out
  and and_12 (and_12_out, BEQ, ZERO);
  not not_1 (not_1_out, decoder_1_out0);
  Priority_Encoder #(.select(2), .disabled(0)) priority_encoder_2 (
    .in0(1'b1), .in1(and_12_out), .in2(JUMP), .in3(1'b0), .out(PCSrc), .en_in(1'b1));  // open: gs, en_out
  Priority_Encoder #(.select(2), .disabled(0)) priority_encoder_3 (
    .in0(not_1_out), .in1(decoder_1_out0), .in2(LUI), .in3(LINK), .out(RegDst));  // open: gs, en_out, en_in
  not not_2 (RS_EN, OP1_IMM12);
  or or_12 (RT_EN, decoder_1_out0, BEQ);
  nor nor_3 (Word_EN, Upper, decoder_1_out6, decoder_1_out8);

  assign MemtoReg = MemRead;
endmodule

module HAZARD_DETECTION_UNIT (
  input  ID_EX_MemRead,
  input  [2:0] IF_ID_RegisterRs,
  input  [2:0] ID_EX_RegisterRd,
  input  [2:0] IF_ID_RegisterRt,
  input  IF_ID_MemWrite,
  input  ID_EX_RegWrite,
  input  EX_MEM_MemRead,
  input  [2:0] EX_MEM_RegisterRd,
  input  IF_ID_JReg,
  input  JUMP,
  input  BEQ,
  input  TAKEN,
  output PCWrite,
  output IF_IDWrite,
  output NOP,
  output IF_FLUSH
);

  wire and_1_out, and_2_out, and_3_out, and_4_out, and_5_out, and_6_out, and_7_out, and_8_out, nand_1_out,
       nand_2_out, or_2_out, or_3_out, or_4_out, or_5_out, or_6_out;
  wire [2:0] xnor_1_out, xnor_2_out, xnor_3_out, xnor_4_out;

  assign xnor_1_out = ~(IF_ID_RegisterRs ^ ID_EX_RegisterRd);  // XNOR_Gate xnor_1, 3 bits wide
  assign xnor_2_out = ~(ID_EX_RegisterRd ^ IF_ID_RegisterRt);  // XNOR_Gate xnor_2, 3 bits wide
  assign xnor_3_out = ~(IF_ID_RegisterRs ^ EX_MEM_RegisterRd);  // XNOR_Gate xnor_3, 3 bits wide
  assign xnor_4_out = ~(EX_MEM_RegisterRd ^ IF_ID_RegisterRt);  // XNOR_Gate xnor_4, 3 bits wide
  or or_1 (IF_FLUSH, JUMP, and_1_out);
  and and_1 (and_1_out, BEQ, TAKEN);
  and and_2 (and_2_out, xnor_1_out[0], xnor_1_out[1], xnor_1_out[2]);
  and and_3 (and_3_out, xnor_2_out[0], xnor_2_out[1], xnor_2_out[2]);
  and and_4 (and_4_out, xnor_3_out[0], xnor_3_out[1], xnor_3_out[2]);
  and and_5 (and_5_out, xnor_4_out[0], xnor_4_out[1], xnor_4_out[2]);
  or or_2 (or_2_out, and_2_out, and_6_out);
  and and_6 (and_6_out, and_3_out, ~IF_ID_MemWrite);  // AND_Gate
  and and_7 (and_7_out, ID_EX_RegWrite, or_3_out);
  or or_3 (or_3_out, and_2_out, and_3_out);
  and and_8 (and_8_out, EX_MEM_MemRead, or_4_out);
  or or_4 (or_4_out, and_4_out, and_5_out);
  or or_5 (or_5_out, IF_ID_JReg, BEQ);
  nand nand_1 (nand_1_out, ID_EX_MemRead, or_2_out);
  or or_6 (or_6_out, and_7_out, and_8_out);
  and and_9 (IF_IDWrite, nand_1_out, nand_2_out);
  nand nand_2 (nand_2_out, or_6_out, or_5_out);
  not not_1 (NOP, IF_IDWrite);

  assign PCWrite = IF_IDWrite;
endmodule

module Final_Circuit (
  input  CLR_PC,
  input  CLR_D,
  input  ENDIANNESS,
  input  CLR_I,
  input  CLR_R
);

  wire alu_1_less, clk_out, comparator_1_eq, control_unit_1_beq, control_unit_1_cas, control_unit_1_extop,
       control_unit_1_jreg, control_unit_1_jump, control_unit_1_link, control_unit_1_memread,
       control_unit_1_memtoreg, control_unit_1_memwrite, control_unit_1_op1_imm12, control_unit_1_regwrite,
       control_unit_1_rs_en, control_unit_1_rt_en, control_unit_1_slt, control_unit_1_upper,
       control_unit_1_word_en, ex_mem_1_memread_2, ex_mem_1_memtoreg_2, ex_mem_1_memwrite_2,
       ex_mem_1_regwrite_2, ex_mem_1_upper_2, ex_mem_1_word_en_2, forwarding_unit_1_ex_forwardop1,
       forwarding_unit_1_ex_forwardop2, forwarding_unit_1_ex_forwardrd, forwarding_unit_1_id_forwardrs,
       forwarding_unit_1_id_forwardrt, forwarding_unit_1_mem_forwarddatain, hazard_detection_unit_1_if_flush,
       hazard_detection_unit_1_if_idwrite, hazard_detection_unit_1_nop, hazard_detection_unit_1_pcwrite,
       id_ex_1_cas_2, id_ex_1_memread_2, id_ex_1_memtoreg_2, id_ex_1_memwrite_2, id_ex_1_rd_valid_2,
       id_ex_1_regwrite_2, id_ex_1_slt_2, id_ex_1_upper_2, id_ex_1_word_en_2, if_id_1_if_flush_2,
       mem_wb_1_memtoreg_2, mem_wb_1_regwrite_2;
  wire [1:0] control_unit_1_op2_imm6, control_unit_1_pcsrc, control_unit_1_regdst, priority_encoder_1_p3;
  wire [2:0] control_unit_1_aluopc, ex_mem_1_rd_index_2, id_ex_1_alu_op_2, id_ex_1_id_ex_rd_4,
       id_ex_1_id_ex_rs_2, id_ex_1_id_ex_rt_2, mem_wb_1_rd_index_2, multiplexer_2_out, multiplexer_3_out,
       multiplexer_4_out;
  wire [3:0] if_id_1_instruction_2_2;
  wire [11:0] if_id_1_instruction_2, multiplexer_8_out;
  wire [15:0] adder_1_out, adder_2_out, alu_1_alu_res, bit_extender_1_out, byte_mirror_1_out,
       dmem_1_data_out, ex_mem_1_alures_2, ex_mem_1_rd_2, extender6_1_extoutput, extender12_1_extoutput,
       forwarding_unit_1_ex_op1_2, forwarding_unit_1_ex_op2_2, forwarding_unit_1_ex_rd,
       forwarding_unit_1_id_rs, forwarding_unit_1_id_rt, forwarding_unit_1_mem_data_in, id_ex_1_id_ex_op1_2,
       id_ex_1_id_ex_op2_2, id_ex_1_id_ex_rd_3, if_id_1_next_pc_2, imem_1_instruction_out,
       mem_wb_1_data_out_2, mem_wb_1_rd_value_2, multiplexer_1_out, multiplexer_5_out, multiplexer_6_out,
       multiplexer_7_out, multiplexer_9_out, multiplexer_10_out, multiplexer_11_out, multiplexer_12_out,
       multiplexer_13_out, multiplexer_14_out, multiplexer_15_out, multiplexer_16_out, multiplexer_17_out,
       PC_q, reg_file_1_read_data_1, reg_file_1_read_data_2;
  wire [15:12] multiplexer_8_out_2;

  Multiplexer #(.select(2), .width(16), .enable("false")) multiplexer_1 (
    .in0(adder_1_out), .in1(adder_2_out), .in2({if_id_1_instruction_2_2, multiplexer_8_out}), .in3(16'h4040),
    .out(multiplexer_1_out), .sel(control_unit_1_pcsrc));
  Clock clk (.out(clk_out));
  Register #(.width(16), .trigger("falling")) PC (
    .D(multiplexer_1_out), .en(hazard_detection_unit_1_pcwrite), .Q(PC_q), .clk(clk_out), .clr(CLR_PC));
  Adder #(.width(16)) adder_1 (.a(PC_q), .b(16'h2), .out(adder_1_out), .cin(1'b0));  // open: cout
  IMEM imem_1 (
    .ADDRESS(PC_q), .MemWrite(1'b0), .MemRead(1'b1), .Clear(CLR_I), .INSTRUCTION_OUT(imem_1_instruction_out),
    .clk(clk_out));  // open: INSTRUCTION_IN
  IF_ID if_id_1 (
    .INSTRUCTION(adder_1_out), .IF_FLUSH(hazard_detection_unit_1_if_flush),
    .IF_ID_WRITE(hazard_detection_unit_1_if_idwrite), .clk(clk_out),
    .INSTRUCTION_2({if_id_1_instruction_2_2, if_id_1_instruction_2}), .IF_FLUSH_2(if_id_1_if_flush_2),
    .NEXT_PC(imem_1_instruction_out), .NEXT_PC_2(if_id_1_next_pc_2));
  EXTENDER6 extender6_1 (
    .Imm6(if_id_1_next_pc_2[5:0]), .ExtOutput(extender6_1_extoutput), .ExtOp(control_unit_1_extop));
  EXTENDER12 extender12_1 (
    .Imm12(if_id_1_next_pc_2[11:0]), .ExtOutput(extender12_1_extoutput), .ExtOp(control_unit_1_extop));
  Multiplexer #(.select(2), .width(3), .enable("false")) multiplexer_2 (
    .in0(if_id_1_next_pc_2[8:6]), .in1(if_id_1_next_pc_2[5:3]), .in2(3'b001), .in3(3'b111),
    .out(multiplexer_2_out), .sel(control_unit_1_regdst));
  HAZARD_DETECTION_UNIT hazard_detection_unit_1 (
    .IF_ID_RegisterRs(if_id_1_next_pc_2[11:9]), .ID_EX_RegisterRd(id_ex_1_id_ex_rd_4),
    .IF_ID_RegisterRt(if_id_1_next_pc_2[8:6]), .PCWrite(hazard_detection_unit_1_pcwrite),
    .IF_IDWrite(hazard_detection_unit_1_if_idwrite), .NOP(hazard_detection_unit_1_nop),
    .JUMP(control_unit_1_jump), .BEQ(control_unit_1_beq), .TAKEN(comparator_1_eq),
    .IF_FLUSH(hazard_detection_unit_1_if_flush), .IF_ID_MemWrite(control_unit_1_memwrite),
    .ID_EX_RegWrite(id_ex_1_regwrite_2), .ID_EX_MemRead(id_ex_1_memread_2), .IF_ID_JReg(control_unit_1_jreg),
    .EX_MEM_RegisterRd(ex_mem_1_rd_index_2), .EX_MEM_MemRead(ex_mem_1_memread_2));
  Multiplexer #(.width(3), .enable("false")) multiplexer_3 (
    .in0(3'b000), .in1(if_id_1_next_pc_2[11:9]), .out(multiplexer_3_out), .sel(control_unit_1_rs_en));
  Multiplexer #(.width(3), .enable("false")) multiplexer_4 (
    .in0(3'b000), .in1(if_id_1_next_pc_2[8:6]), .out(multiplexer_4_out), .sel(control_unit_1_rt_en));
  REG_FILE reg_file_1 (
    .Write_data(multiplexer_17_out), .read_data_1(reg_file_1_read_data_1),
    .read_data_2(reg_file_1_read_data_2), .Write_register(mem_wb_1_rd_index_2),
    .RegWrite(mem_wb_1_regwrite_2), .clk(clk_out), .read_register_1(if_id_1_next_pc_2[11:9]),
    .read_register_2(if_id_1_next_pc_2[8:6]), .Clear(CLR_R));
  Adder #(.width(16)) adder_2 (
    .a(multiplexer_7_out), .b({if_id_1_instruction_2_2, if_id_1_instruction_2}), .out(adder_2_out), .cin(1'b0));  // open: cout
  Multiplexer #(.width(16), .enable("false")) multiplexer_5 (
    .in0(reg_file_1_read_data_1), .in1(forwarding_unit_1_id_rs), .out(multiplexer_5_out),
    .sel(forwarding_unit_1_id_forwardrs));
  Multiplexer #(.width(16), .enable("false")) multiplexer_6 (
    .in0(reg_file_1_read_data_2), .in1(forwarding_unit_1_id_rt), .out(multiplexer_6_out),
    .sel(forwarding_unit_1_id_forwardrt));
  Comparator #(.width(16), .mode("unsigned")) comparator_1 (
    .a(multiplexer_5_out), .b(multiplexer_6_out), .eq(comparator_1_eq));  // open: gt, lt
  CONTROL_UNIT control_unit_1 (
    .Instruction(if_id_1_next_pc_2), .AluOpc(control_unit_1_aluopc), .RegWrite(control_unit_1_regwrite),
    .ExtOp(control_unit_1_extop), .OP1_IMM12(control_unit_1_op1_imm12), .JUMP(control_unit_1_jump),
    .MemWrite(control_unit_1_memwrite), .MemtoReg(control_unit_1_memtoreg), .MemRead(control_unit_1_memread),
    .IF_flush(if_id_1_if_flush_2), .OP2_IMM6(control_unit_1_op2_imm6[0]), .BEQ(control_unit_1_beq),
    .PCSrc(control_unit_1_pcsrc), .LUI(control_unit_1_op2_imm6[1]), .RegDst(control_unit_1_regdst),
    .SLT(control_unit_1_slt), .CAS(control_unit_1_cas), .RT_EN(control_unit_1_rt_en),
    .RS_EN(control_unit_1_rs_en), .LINK(control_unit_1_link), .ZERO(comparator_1_eq),
    .Word_EN(control_unit_1_word_en), .Upper(control_unit_1_upper), .JReg(control_unit_1_jreg));
  Multiplexer #(.select(2), .width(16), .enable("false")) multiplexer_7 (
    .in0(multiplexer_6_out), .in1(extender6_1_extoutput), .in2(16'h4), .in3({16{1'b0}}),
    .out(multiplexer_7_out), .sel(control_unit_1_op2_imm6));
  Multiplexer #(.width(16), .enable("false")) multiplexer_8 (
    .in0(multiplexer_5_out), .in1(extender12_1_extoutput), .out({multiplexer_8_out_2, multiplexer_8_out}),
    .sel(control_unit_1_op1_imm12));
  ID_EX id_ex_1 (
    .ID_EX_Write(1'b1), .ALU_OP(control_unit_1_aluopc), .MemtoReg(control_unit_1_memtoreg),
    .MemWrite(control_unit_1_memwrite), .MemRead(control_unit_1_memread), .RegWrite(control_unit_1_regwrite),
    .RD_valid(control_unit_1_link), .ID_EX_OP1({multiplexer_8_out_2, multiplexer_8_out}),
    .ID_EX_OP2(multiplexer_7_out), .ID_EX_RS(multiplexer_3_out), .ID_EX_RT(multiplexer_4_out),
    .ID_EX_RD_2(multiplexer_2_out), .clk(clk_out), .ID_EX_OP1_2(id_ex_1_id_ex_op1_2),
    .ID_EX_OP2_2(id_ex_1_id_ex_op2_2), .ID_EX_RS_2(id_ex_1_id_ex_rs_2), .ID_EX_RT_2(id_ex_1_id_ex_rt_2),
    .ID_EX_RD_4(id_ex_1_id_ex_rd_4), .NOP(hazard_detection_unit_1_nop), .ID_EX_RD_3(id_ex_1_id_ex_rd_3),
    .ID_EX_RD(multiplexer_9_out), .SLT(control_unit_1_slt), .CAS(control_unit_1_cas),
    .ALU_OP_2(id_ex_1_alu_op_2), .MemtoReg_2(id_ex_1_memtoreg_2), .MemWrite_2(id_ex_1_memwrite_2),
    .MemRead_2(id_ex_1_memread_2), .RegWrite_2(id_ex_1_regwrite_2), .SLT_2(id_ex_1_slt_2),
    .CAS_2(id_ex_1_cas_2), .RD_valid_2(id_ex_1_rd_valid_2), .WORD_EN(control_unit_1_word_en),
    .WORD_EN_2(id_ex_1_word_en_2), .Upper(control_unit_1_upper), .Upper_2(id_ex_1_upper_2));
  Multiplexer #(.width(16), .enable("false")) multiplexer_9 (
    .in0({if_id_1_instruction_2_2, if_id_1_instruction_2}), .in1(multiplexer_6_out), .out(multiplexer_9_out),
    .sel(control_unit_1_op2_imm6[0]));
  Multiplexer #(.width(16), .disabled(0), .enable("false")) multiplexer_10 (
    .in0(id_ex_1_id_ex_op1_2), .in1(forwarding_unit_1_ex_op1_2), .out(multiplexer_10_out),
    .sel(forwarding_unit_1_ex_forwardop1));
  Multiplexer #(.width(16), .disabled(0), .enable("false")) multiplexer_11 (
    .in0(id_ex_1_id_ex_op2_2), .in1(forwarding_unit_1_ex_op2_2), .out(multiplexer_11_out),
    .sel(forwarding_unit_1_ex_forwardop2));
  ALU alu_1 (
    .OPERATION(id_ex_1_alu_op_2), .OPERAND_1(multiplexer_10_out), .OPERAND_2(multiplexer_11_out),
    .ALU_RES(alu_1_alu_res), .less(alu_1_less));  // open: carry, borrow, greater, zero
  Multiplexer #(.width(16), .disabled(0), .enable("false")) multiplexer_12 (
    .in0(id_ex_1_id_ex_rd_3), .in1(forwarding_unit_1_ex_rd), .out(multiplexer_12_out),
    .sel(forwarding_unit_1_ex_forwardrd));
  assign bit_extender_1_out = {{15{1'b0}}, alu_1_less};  // Bit_Extender bit_extender_1
  Multiplexer #(.width(16), .enable("false")) multiplexer_13 (
    .in0(multiplexer_10_out), .in1(multiplexer_11_out), .out(multiplexer_13_out), .sel(alu_1_less));
  FORWARDING_UNIT forwarding_unit_1 (
    .MEM_WB_RegWrite(mem_wb_1_regwrite_2), .MEM_WB_RegisterRd(mem_wb_1_rd_index_2),
    .ID_RegisterRs(multiplexer_3_out), .ID_RegisterRt(multiplexer_4_out),
    .EX_MEM_RegWrite(ex_mem_1_regwrite_2), .EX_MEM_RegisterRd(ex_mem_1_rd_index_2),
    .ID_ForwardRs(forwarding_unit_1_id_forwardrs), .ID_ForwardRt(forwarding_unit_1_id_forwardrt),
    .MEM_WB_Rd(multiplexer_17_out), .EX_MEM_Rd(multiplexer_16_out), .ID_Rs(forwarding_unit_1_id_rs),
    .ID_Rt(forwarding_unit_1_id_rt), .EX_MEM_MemWrite(ex_mem_1_memwrite_2),
    .EX_MEM_MemRead(ex_mem_1_memread_2), .EX_OP1(id_ex_1_id_ex_rs_2), .EX_OP2(id_ex_1_id_ex_rt_2),
    .EX_ForwardOP1(forwarding_unit_1_ex_forwardop1), .EX_ForwardOP2(forwarding_unit_1_ex_forwardop2),
    .EX_OP1_2(forwarding_unit_1_ex_op1_2), .EX_OP2_2(forwarding_unit_1_ex_op2_2),
    .MEM_DATA_IN(forwarding_unit_1_mem_data_in), .MEM_ForwardDataIn(forwarding_unit_1_mem_forwarddatain),
    .EX_RegisterRd(id_ex_1_id_ex_rd_4), .EX_MemWrite(id_ex_1_memwrite_2),
    .EX_ForwardRD(forwarding_unit_1_ex_forwardrd), .EX_RD(forwarding_unit_1_ex_rd));
  // Priority_Encoder #(.select(2)) priority_encoder_1: pin names not known; wires that end beside it: 1'b1, id_ex_1_slt_2, priority_encoder_1_p3, id_ex_1_cas_2, id_ex_1_rd_valid_2, 1'b1
  Multiplexer #(.select(2), .width(16), .enable("false")) multiplexer_14 (
    .in0(alu_1_alu_res), .in1(bit_extender_1_out), .in2(multiplexer_13_out), .in3(multiplexer_12_out),
    .out(multiplexer_14_out), .sel(priority_encoder_1_p3));
  EX_MEM ex_mem_1 (
    .enable(1'b1), .MemtoReg(id_ex_1_memtoreg_2), .MemWrite(id_ex_1_memwrite_2), .MemRead(id_ex_1_memread_2),
    .RegWrite(id_ex_1_regwrite_2), .ALURes(multiplexer_14_out), .Rd(multiplexer_12_out), .clk(clk_out),
    .MemtoReg_2(ex_mem_1_memtoreg_2), .MemWrite_2(ex_mem_1_memwrite_2), .MemRead_2(ex_mem_1_memread_2),
    .RegWrite_2(ex_mem_1_regwrite_2), .ALURes_2(ex_mem_1_alures_2), .Rd_2(ex_mem_1_rd_2),
    .WORD_EN(id_ex_1_word_en_2), .WORD_EN_2(ex_mem_1_word_en_2), .Rd_index(id_ex_1_id_ex_rd_4),
    .Rd_index_2(ex_mem_1_rd_index_2), .Upper(id_ex_1_upper_2), .Upper_2(ex_mem_1_upper_2));
  Multiplexer #(.width(16), .enable("false")) multiplexer_15 (
    .in0(ex_mem_1_rd_2), .in1(forwarding_unit_1_mem_data_in), .out(multiplexer_15_out),
    .sel(forwarding_unit_1_mem_forwarddatain));
  Multiplexer #(.width(16), .enable("false")) multiplexer_16 (
    .in0(ex_mem_1_alures_2), .in1(multiplexer_15_out), .out(multiplexer_16_out), .sel(ex_mem_1_memwrite_2));
  DMEM dmem_1 (
    .ADDRESS(ex_mem_1_alures_2), .MemWrite(ex_mem_1_memwrite_2), .MemRead(ex_mem_1_memread_2), .Clear(CLR_D),
    .WORD_EN(ex_mem_1_word_en_2), .DATA_IN(multiplexer_16_out), .ENDIANNESS(ENDIANNESS),
    .DATA_OUT(dmem_1_data_out), .clk(clk_out));
  MEM_WB mem_wb_1 (
    .MemToReg(ex_mem_1_memtoreg_2), .RegWrite(ex_mem_1_regwrite_2), .DATA_OUT(byte_mirror_1_out),
    .Rd_value(multiplexer_16_out), .Rd_index(ex_mem_1_rd_index_2), .MemToReg_2(mem_wb_1_memtoreg_2),
    .RegWrite_2(mem_wb_1_regwrite_2), .DATA_OUT_2(mem_wb_1_data_out_2), .Rd_value_2(mem_wb_1_rd_value_2),
    .Rd_index_2(mem_wb_1_rd_index_2), .enable(1'b1), .clk(clk_out));
  BYTE_MIRROR byte_mirror_1 (.IN(dmem_1_data_out), .EN(ex_mem_1_upper_2), .OUT(byte_mirror_1_out));
  Multiplexer #(.width(16), .enable("false")) multiplexer_17 (
    .in0(mem_wb_1_rd_value_2), .in1(mem_wb_1_data_out_2), .out(multiplexer_17_out), .sel(mem_wb_1_memtoreg_2));
endmodule

module IF_ID (
  input  IF_ID_WRITE,
  input  [15:0] NEXT_PC,
  input  [15:0] INSTRUCTION,
  input  IF_FLUSH,
  input  clk,
  output [15:0] NEXT_PC_2,
  output [15:0] INSTRUCTION_2,
  output IF_FLUSH_2
);

  Register #(.width(16), .trigger("falling")) register_1 (
    .D(NEXT_PC), .en(IF_ID_WRITE), .Q(NEXT_PC_2), .clk(clk), .clr(1'b0));
  Register #(.width(16), .trigger("falling")) register_2 (
    .D(INSTRUCTION), .en(IF_ID_WRITE), .Q(INSTRUCTION_2), .clk(clk), .clr(1'b0));
  Register #(.width(1), .trigger("falling")) register_3 (
    .D(IF_FLUSH), .en(IF_ID_WRITE), .Q(IF_FLUSH_2), .clk(clk), .clr(1'b0));
endmodule

module EXTENDER12 (
  input  [11:0] Imm12,
  input  ExtOp,
  output [15:0] ExtOutput
);

  wire [15:0] bit_extender_1_out, bit_extender_2_out;

  assign bit_extender_1_out = {{4{1'b0}}, Imm12};  // Bit_Extender bit_extender_1
  assign bit_extender_2_out = {{4{Imm12[11]}}, Imm12};  // Bit_Extender bit_extender_2
  Multiplexer #(.width(16), .enable("false")) multiplexer_1 (
    .in0(bit_extender_1_out), .in1(bit_extender_2_out), .out(ExtOutput), .sel(ExtOp));
endmodule

module ID_EX (
  input  ID_EX_Write,
  input  NOP,
  input  [2:0] ALU_OP,
  input  Upper,
  input  MemtoReg,
  input  MemWrite,
  input  MemRead,
  input  RegWrite,
  input  SLT,
  input  CAS,
  input  RD_valid,
  input  WORD_EN,
  input  [15:0] ID_EX_OP1,
  input  [15:0] ID_EX_OP2,
  input  [15:0] ID_EX_RD,
  input  [2:0] ID_EX_RS,
  input  [2:0] ID_EX_RT,
  input  [2:0] ID_EX_RD_2,
  input  clk,
  output [2:0] ALU_OP_2,
  output Upper_2,
  output MemtoReg_2,
  output MemWrite_2,
  output MemRead_2,
  output RegWrite_2,
  output SLT_2,
  output CAS_2,
  output RD_valid_2,
  output WORD_EN_2,
  output [15:0] ID_EX_OP1_2,
  output [15:0] ID_EX_OP2_2,
  output [15:0] ID_EX_RD_3,
  output [2:0] ID_EX_RS_2,
  output [2:0] ID_EX_RT_2,
  output [2:0] ID_EX_RD_4
);

  wire multiplexer_2_out, multiplexer_3_out, multiplexer_4_out, multiplexer_5_out, multiplexer_6_out,
       multiplexer_7_out, multiplexer_8_out, multiplexer_9_out, multiplexer_10_out;
  wire [2:0] multiplexer_1_out, multiplexer_14_out, multiplexer_15_out, multiplexer_16_out;
  wire [15:0] multiplexer_11_out, multiplexer_12_out, multiplexer_13_out;

  Multiplexer #(.width(3), .enable("false")) multiplexer_1 (
    .in0(ALU_OP), .in1(3'b000), .out(multiplexer_1_out), .sel(NOP));
  Multiplexer #(.enable("false")) multiplexer_2 (.in0(Upper), .in1(1'b0), .out(multiplexer_2_out), .sel(NOP));
  Multiplexer #(.enable("false")) multiplexer_3 (.in0(MemtoReg), .in1(1'b0), .out(multiplexer_3_out), .sel(NOP));
  Multiplexer #(.enable("false")) multiplexer_4 (.in0(MemWrite), .in1(1'b0), .out(multiplexer_4_out), .sel(NOP));
  Multiplexer #(.enable("false")) multiplexer_5 (.in0(MemRead), .in1(1'b0), .out(multiplexer_5_out), .sel(NOP));
  Multiplexer #(.enable("false")) multiplexer_6 (.in0(RegWrite), .in1(1'b0), .out(multiplexer_6_out), .sel(NOP));
  Multiplexer #(.enable("false")) multiplexer_7 (.in0(SLT), .in1(1'b0), .out(multiplexer_7_out), .sel(NOP));
  Multiplexer #(.enable("false")) multiplexer_8 (.in0(CAS), .in1(1'b0), .out(multiplexer_8_out), .sel(NOP));
  Multiplexer #(.enable("false")) multiplexer_9 (.in0(RD_valid), .in1(1'b0), .out(multiplexer_9_out), .sel(NOP));
  Multiplexer #(.enable("false")) multiplexer_10 (.in0(WORD_EN), .in1(1'b0), .out(multiplexer_10_out), .sel(NOP));
  Multiplexer #(.width(16), .enable("false")) multiplexer_11 (
    .in0(ID_EX_OP1), .in1({16{1'b0}}), .out(multiplexer_11_out), .sel(NOP));
  Multiplexer #(.width(16), .enable("false")) multiplexer_12 (
    .in0(ID_EX_OP2), .in1({16{1'b0}}), .out(multiplexer_12_out), .sel(NOP));
  Multiplexer #(.width(16), .enable("false")) multiplexer_13 (
    .in0(ID_EX_RD), .in1({16{1'b0}}), .out(multiplexer_13_out), .sel(NOP));
  Multiplexer #(.width(3), .enable("false")) multiplexer_14 (
    .in0(ID_EX_RS), .in1(3'b000), .out(multiplexer_14_out), .sel(NOP));
  Multiplexer #(.width(3), .enable("false")) multiplexer_15 (
    .in0(ID_EX_RT), .in1(3'b000), .out(multiplexer_15_out), .sel(NOP));
  Multiplexer #(.width(3), .enable("false")) multiplexer_16 (
    .in0(ID_EX_RD_2), .in1(3'b000), .out(multiplexer_16_out), .sel(NOP));
  Register #(.width(3), .trigger("falling")) register_1 (
    .D(multiplexer_1_out), .en(ID_EX_Write), .Q(ALU_OP_2), .clk(clk), .clr(1'b0));
  Register #(.width(1), .trigger("falling")) register_2 (
    .D(multiplexer_2_out), .en(ID_EX_Write), .Q(Upper_2), .clk(clk), .clr(1'b0));
  Register #(.width(1), .trigger("falling")) register_3 (
    .D(multiplexer_3_out), .en(ID_EX_Write), .Q(MemtoReg_2), .clk(clk), .clr(1'b0));
  Register #(.width(1), .trigger("falling")) register_4 (
    .D(multiplexer_4_out), .en(ID_EX_Write), .Q(MemWrite_2), .clk(clk), .clr(1'b0));
  Register #(.width(1), .trigger("falling")) register_5 (
    .D(multiplexer_5_out), .en(ID_EX_Write), .Q(MemRead_2), .clk(clk), .clr(1'b0));
  Register #(.width(1), .trigger("falling")) register_6 (
    .D(multiplexer_6_out), .en(ID_EX_Write), .Q(RegWrite_2), .clk(clk), .clr(1'b0));
  Register #(.width(1), .trigger("falling")) register_7 (
    .D(multiplexer_7_out), .en(ID_EX_Write), .Q(SLT_2), .clk(clk), .clr(1'b0));
  Register #(.width(1), .trigger("falling")) register_8 (
    .D(multiplexer_8_out), .en(ID_EX_Write), .Q(CAS_2), .clk(clk), .clr(1'b0));
  Register #(.width(1), .trigger("falling")) register_9 (
    .D(multiplexer_9_out), .en(ID_EX_Write), .Q(RD_valid_2), .clk(clk), .clr(1'b0));
  Register #(.width(1), .trigger("falling")) register_10 (
    .D(multiplexer_10_out), .en(ID_EX_Write), .Q(WORD_EN_2), .clk(clk), .clr(1'b0));
  Register #(.width(16), .trigger("falling")) register_11 (
    .D(multiplexer_11_out), .en(ID_EX_Write), .Q(ID_EX_OP1_2), .clk(clk), .clr(1'b0));
  Register #(.width(16), .trigger("falling")) register_12 (
    .D(multiplexer_12_out), .Q(ID_EX_OP2_2), .clk(clk), .clr(1'b0));  // open: en
  Register #(.width(16), .trigger("falling")) register_13 (
    .D(multiplexer_13_out), .en(ID_EX_Write), .Q(ID_EX_RD_3), .clk(clk), .clr(1'b0));
  Register #(.width(3), .trigger("falling")) register_14 (
    .D(multiplexer_14_out), .en(ID_EX_Write), .Q(ID_EX_RS_2), .clk(clk), .clr(1'b0));
  Register #(.width(3), .trigger("falling")) register_15 (
    .D(multiplexer_15_out), .Q(ID_EX_RT_2), .clk(clk), .clr(1'b0));  // open: en
  Register #(.width(3), .trigger("falling")) register_16 (
    .D(multiplexer_16_out), .Q(ID_EX_RD_4), .clk(clk), .clr(1'b0));  // open: en
endmodule

module EX_MEM (
  input  enable,
  input  Upper,
  input  MemtoReg,
  input  MemWrite,
  input  MemRead,
  input  RegWrite,
  input  WORD_EN,
  input  [15:0] ALURes,
  input  [15:0] Rd,
  input  [2:0] Rd_index,
  input  clk,
  output Upper_2,
  output MemtoReg_2,
  output MemWrite_2,
  output MemRead_2,
  output RegWrite_2,
  output WORD_EN_2,
  output [15:0] ALURes_2,
  output [15:0] Rd_2,
  output [2:0] Rd_index_2
);

  Register #(.width(1), .trigger("falling")) register_1 (.D(Upper), .en(enable), .Q(Upper_2), .clk(clk), .clr(1'b0));
  Register #(.width(5), .trigger("falling")) register_2 (
    .D({WORD_EN, RegWrite, MemRead, MemWrite, MemtoReg}), .en(enable),
    .Q({WORD_EN_2, RegWrite_2, MemRead_2, MemWrite_2, MemtoReg_2}), .clk(clk), .clr(1'b0));
  Register #(.width(32), .trigger("falling")) register_3 (
    .D({Rd, ALURes}), .en(enable), .Q({Rd_2, ALURes_2}), .clk(clk), .clr(1'b0));
  Register #(.width(3), .trigger("falling")) register_4 (
    .D(Rd_index), .en(enable), .Q(Rd_index_2), .clk(clk), .clr(1'b0));
endmodule

module MEM_WB (
  input  enable,
  input  MemToReg,
  input  RegWrite,
  input  [15:0] DATA_OUT,
  input  [15:0] Rd_value,
  input  [2:0] Rd_index,
  input  clk,
  output MemToReg_2,
  output RegWrite_2,
  output [15:0] DATA_OUT_2,
  output [15:0] Rd_value_2,
  output [2:0] Rd_index_2
);

  Register #(.width(1), .trigger("falling")) register_1 (
    .D(MemToReg), .en(enable), .Q(MemToReg_2), .clk(clk), .clr(1'b0));
  Register #(.width(1), .trigger("falling")) register_2 (
    .D(RegWrite), .en(enable), .Q(RegWrite_2), .clk(clk), .clr(1'b0));
  Register #(.width(16), .trigger("falling")) register_3 (
    .D(DATA_OUT), .en(enable), .Q(DATA_OUT_2), .clk(clk), .clr(1'b0));
  Register #(.width(16), .trigger("falling")) register_4 (
    .D(Rd_value), .en(enable), .Q(Rd_value_2), .clk(clk), .clr(1'b0));
  Register #(.width(3), .trigger("falling")) register_5 (
    .D(Rd_index), .en(enable), .Q(Rd_index_2), .clk(clk), .clr(1'b0));
endmodule
