// Logisim project pipelined-data-path.circ as structural Verilog: 6 circuits, main circuit main
module main (
  input  [5:0] Imm6,
  input  ExtOp,
  output [15:0] ExtOutput
);

  extender extender_1 (.Imm6(Imm6), .ExtOp(ExtOp), .ExtOutput(ExtOutput));
  _16_bit_register_file u_16_bit_register_file_1 ();  // open: Write_data, Write_register, RegWrite, read_register_2, read_register_1, read_data_1, read_data_2, clk
endmodule

// 16-bit register file
module _16_bit_register_file (
  input  [2:0] read_register_1,
  input  [2:0] Write_register,
  input  [15:0] Write_data,
  input  [2:0] read_register_2,
  input  RegWrite,
  input  clk,
  output [15:0] read_data_1,
  output [15:0] read_data_2
);

  wire and_1_out, and_2_out, and_3_out, and_4_out, and_5_out, and_6_out, and_7_out, and_8_out,
       decoder_1_out0, decoder_1_out1, decoder_1_out2, decoder_1_out3, decoder_1_out4, decoder_1_out5,
       decoder_1_out6, decoder_1_out7;
  wire [15:0] register_1_q, register_2_q, register_3_q, register_4_q, register_5_q, register_6_q,
       register_7_q, register_8_q;

  Decoder #(.select(3)) decoder_1 (
    .out0(decoder_1_out0), .out1(decoder_1_out1), .out2(decoder_1_out2), .out3(decoder_1_out3),
    .out4(decoder_1_out4), .out5(decoder_1_out5), .out6(decoder_1_out6), .out7(decoder_1_out7),
    .sel(Write_register));  // open: en
  and and_1 (and_1_out, decoder_1_out0, RegWrite);
  and and_2 (and_2_out, decoder_1_out1, RegWrite);
  and and_3 (and_3_out, decoder_1_out2, RegWrite);
  and and_4 (and_4_out, decoder_1_out3, RegWrite);
  and and_5 (and_5_out, decoder_1_out4, RegWrite);
  and and_6 (and_6_out, decoder_1_out5, RegWrite);
  and and_7 (and_7_out, decoder_1_out6, RegWrite);
  and and_8 (and_8_out, decoder_1_out7, RegWrite);
  Register #(.width(16)) register_1 (.D({16{1'b0}}), .Q(register_1_q), .clk(clk), .clr(and_1_out));  // open: en
  Register #(.width(16)) register_2 (.D(Write_data), .Q(register_2_q), .clk(clk), .clr(and_2_out));  // open: en
  Register #(.width(16)) register_3 (.D(Write_data), .Q(register_3_q), .clk(clk), .clr(and_3_out));  // open: en
  Register #(.width(16)) register_4 (.D(Write_data), .Q(register_4_q), .clk(clk), .clr(and_4_out));  // open: en
  Register #(.width(16)) register_5 (.D(Write_data), .Q(register_5_q), .clk(clk), .clr(and_5_out));  // open: en
  Register #(.width(16)) register_6 (.D(Write_data), .Q(register_6_q), .clk(clk), .clr(and_6_out));  // open: en
  Register #(.width(16)) register_7 (.D(Write_data), .Q(register_7_q), .clk(clk), .clr(and_7_out));  // open: en
  Register #(.width(16)) register_8 (.D(Write_data), .Q(register_8_q), .clk(clk), .clr(and_8_out));  // open: en
  Multiplexer #(.select(3), .width(16)) multiplexer_1 (
    .in0(register_1_q), .in1(register_2_q), .in2(register_3_q), .in3(register_4_q), .in4(register_5_q),
    .in5(register_6_q), .in6(register_7_q), .in7(register_8_q), .out(read_data_1), .sel(read_register_1));  // open: en
  Multiplexer #(.select(3), .width(16)) multiplexer_2 (
    .in0(register_1_q), .in1(register_2_q), .in2(register_3_q), .in3(register_4_q), .in4(register_5_q),
    .in5(register_6_q), .in6(register_7_q), .in7(register_8_q), .out(read_data_2), .sel(read_register_2));  // open: en
endmodule

// Extender
module extender (
  input  [5:0] Imm6,
  input  ExtOp,
  output [15:0] ExtOutput
);

  wire [15:0] bit_extender_1_out, bit_extender_2_out;

  assign bit_extender_1_out = {{10{1'b0}}, Imm6};  // Bit_Extender bit_extender_1
  assign bit_extender_2_out = {{10{Imm6[5]}}, Imm6};  // Bit_Extender bit_extender_2
  Multiplexer #(.width(16)) multiplexer_1 (
    .in0(bit_extender_1_out), .in1(bit_extender_2_out), .out(ExtOutput), .sel(ExtOp));  // open: en
endmodule

module forwarding_unit (
  input  EX_MEM_RegWrite,
  input  [2:0] ID_EX_RegisterRs,
  input  [2:0] EX_MEM_RegisterRd,
  input  [2:0] ID_EX_RegisterRt,
  input  MEM_WB_RegWrite,
  input  [2:0] MEM_WB_RegisterRd,
  output [1:0] ForwardA,
  output [1:0] ForwardB
);

  wire and_1_out, and_2_out, and_3_out, and_4_out, and_5_out, and_6_out, and_7_out, and_8_out, or_1_out,
       or_2_out;
  wire [2:0] xnor_1_out, xnor_2_out, xnor_3_out, xnor_4_out, xor_1_out, xor_2_out;

  assign xor_1_out = 3'b000 ^ MEM_WB_RegisterRd;  // XOR_Gate xor_1, 3 bits wide
  assign xnor_1_out = ~(ID_EX_RegisterRs ^ MEM_WB_RegisterRd);  // XNOR_Gate xnor_1, 3 bits wide
  assign xnor_2_out = ~(ID_EX_RegisterRt ^ MEM_WB_RegisterRd);  // XNOR_Gate xnor_2, 3 bits wide
  assign xnor_3_out = ~(ID_EX_RegisterRs ^ EX_MEM_RegisterRd);  // XNOR_Gate xnor_3, 3 bits wide
  assign xor_2_out = EX_MEM_RegisterRd ^ 3'b000;  // XOR_Gate xor_2, 3 bits wide
  assign xnor_4_out = ~(ID_EX_RegisterRt ^ EX_MEM_RegisterRd);  // XNOR_Gate xnor_4, 3 bits wide
  and and_1 (and_1_out, xnor_3_out[0], xnor_3_out[1], xnor_3_out[2]);
  or or_1 (or_1_out, xor_2_out[0], xor_2_out[1], xor_2_out[2]);
  and and_2 (and_2_out, xnor_4_out[0], xnor_4_out[1], xnor_4_out[2]);
  or or_2 (or_2_out, xor_1_out[0], xor_1_out[1], xor_1_out[2]);
  and and_3 (and_3_out, xnor_1_out[0], xnor_1_out[1], xnor_1_out[2]);
  and and_4 (and_4_out, xnor_2_out[0], xnor_2_out[1], xnor_2_out[2]);
  and and_5 (and_5_out, EX_MEM_RegWrite, or_1_out, and_1_out);
  and and_6 (and_6_out, EX_MEM_RegWrite, or_1_out, and_2_out);
  and and_7 (and_7_out, MEM_WB_RegWrite, or_2_out, and_3_out);
  and and_8 (and_8_out, MEM_WB_RegWrite, or_2_out, and_4_out);
  Priority_Encoder #(.select(2)) priority_encoder_1 (
    .in1(and_7_out), .in2(and_5_out), .out(ForwardA));  // open: in0, in3, gs, en_out, en_in
  Priority_Encoder #(.select(2)) priority_encoder_2 (
    .in1(and_8_out), .in2(and_6_out), .out(ForwardB));  // open: in0, in3, gs, en_out, en_in
endmodule

module control_unit (
  input  [15:0] Instruction_Encoding,
  output ExtOp,
  output r_type,
  output RegWrite,
  output RegDst,
  output MemtoReg,
  output MemRead,
  output MemWrite,
  output checkImm,
  output BEQ,
  output J,
  output checkR,
  output ALUSrc,
  output [2:0] ALUop,
  output checkL
);

  wire and_1_out, and_2_out, and_3_out, and_4_out, and_5_out, and_6_out, and_7_out, and_8_out, and_9_out,
       decoder_1_out0, decoder_1_out2, decoder_1_out3, decoder_1_out6, decoder_1_out7, decoder_2_out1,
       decoder_2_out2, decoder_2_out3, decoder_2_out11, or_1_out, or_2_out, or_3_out;
  wire [2:0] xnor_1_out, xnor_2_out, xnor_3_out;

  assign xnor_1_out = ~(3'b000 ^ Instruction_Encoding[9:7]);  // XNOR_Gate xnor_1, 3 bits wide
  assign xnor_2_out = ~(Instruction_Encoding[9:7] ^ 3'b001);  // XNOR_Gate xnor_2, 3 bits wide
  assign xnor_3_out = ~(Instruction_Encoding[12:10] ^ 3'b000);  // XNOR_Gate xnor_3, 3 bits wide
  Decoder #(.select(3)) decoder_1 (
    .out0(decoder_1_out0), .out2(decoder_1_out2), .out3(decoder_1_out3), .out6(decoder_1_out6),
    .out7(decoder_1_out7), .sel(Instruction_Encoding[15:13]));  // open: out1, out4, out5, en
  and and_1 (and_1_out, xnor_1_out[0], xnor_1_out[1], xnor_1_out[2]);
  and and_2 (and_2_out, xnor_2_out[1], xnor_2_out[0], xnor_2_out[2]);
  and and_3 (and_3_out, xnor_3_out[0], xnor_3_out[2]);
  and and_4 (and_4_out, r_type, decoder_1_out7);
  and and_5 (and_5_out, decoder_1_out3, r_type);
  and and_6 (and_6_out, r_type, decoder_1_out2);
  and and_7 (and_7_out, decoder_1_out6, r_type);
  Decoder #(.select(4)) decoder_2 (
    .out0(r_type), .out1(decoder_2_out1), .out2(decoder_2_out2), .out3(decoder_2_out3), .out4(MemRead),
    .out7(MemWrite), .out9(BEQ), .out10(J), .out11(decoder_2_out11), .sel(Instruction_Encoding[3:0]));  // open: out5, out6, out8, out12, out13, out14, out15, en
  or or_1 (or_1_out, and_4_out, decoder_2_out1);
  or or_2 (or_2_out, decoder_2_out3, and_5_out);
  or or_3 (or_3_out, and_7_out, decoder_2_out2);
  Priority_Encoder priority_encoder_1 (
    .in0(or_1_out), .in1(or_3_out), .in2(or_2_out), .in3(and_6_out), .in4(BEQ), .out(ALUop));  // open: in5, in6, in7, en_in, gs, en_out
  or or_4 (checkImm, J, decoder_2_out11);
  and and_8 (and_8_out, r_type, decoder_1_out0, and_1_out, and_3_out);
  or or_5 (checkR, and_8_out, and_9_out);
  and and_9 (and_9_out, r_type, decoder_1_out0, and_3_out, and_2_out);
  or or_6 (checkL, decoder_2_out11, and_9_out);
  nor nor_1 (ExtOp, decoder_2_out1, decoder_2_out2);
  nor nor_2 (RegWrite, MemWrite, J, BEQ);
  nor nor_3 (ALUSrc, decoder_2_out1, BEQ);

  assign MemtoReg = MemRead;
  assign RegDst = r_type;
endmodule

module hazard_detection_unit (
  input  ID_EX_MemRead,
  input  [2:0] IF_ID_RegisterRs,
  input  [2:0] ID_EX_RegisterRt,
  input  [2:0] IF_ID_RegisterRt,
  output PCWrite,
  output IF_IDWrite,
  output MuxSelectionBit
);

  wire and_1_out, and_2_out, or_1_out;
  wire [2:0] xnor_1_out, xnor_2_out;

  assign xnor_1_out = ~(IF_ID_RegisterRs ^ ID_EX_RegisterRt);  // XNOR_Gate xnor_1, 3 bits wide
  assign xnor_2_out = ~(ID_EX_RegisterRt ^ IF_ID_RegisterRt);  // XNOR_Gate xnor_2, 3 bits wide
  and and_1 (and_1_out, xnor_1_out[0], xnor_1_out[1], xnor_1_out[2]);
  and and_2 (and_2_out, xnor_2_out[0], xnor_2_out[1], xnor_2_out[2]);
  or or_1 (or_1_out, and_1_out, and_2_out);
  nand nand_1 (IF_IDWrite, ID_EX_MemRead, or_1_out);

  assign MuxSelectionBit = IF_IDWrite;
  assign PCWrite = IF_IDWrite;
endmodule
